# Fritzing sketch hardware (saved by Fritzing 0.9.5d)
breadboards: 1

parts:
  Part1 = Arduino Uno (Rev3) - ICSP  # not connected
  Pololu_A1 = Pololu A4988 [package=SO16]
  Part2 = Arduino Motor Shield
  M1 = Stepper Motor - Bipolar
  S1 = SPST Switch [package=switche-dpdt]  # not connected
  J3 = Basic Servo  # not connected
  J2 = Basic Servo  # not connected
  VCC1 = 4 x AAA Battery Mount  # not connected
  J1 = Basic Servo

nets:
  N1: Pololu_A1.ENABLE, Part2.N$345
  N2: Pololu_A1.MS1, Part2.N$344
  N3: Pololu_A1.MS2, Part2.N$343
  N4: Pololu_A1.MS3, Part2.N$342
  N5: Pololu_A1.RESET, Part2.N$341
  N6: Pololu_A1.SLEEP, Part2.N$340
  N7: Pololu_A1.STEP, Part2.N$339
  N8: Pololu_A1.DIR, Part2.N$354
  N9: Pololu_A1.GND#8, Part2.N$157
  N10: Pololu_A1.VDD, Part2.N$183
  N11: Pololu_A1.1B, Part2.N$209
  N12: Pololu_A1.1A, Part2.N$235
  N13: Pololu_A1.2A, Part2.N$261
  N14: Pololu_A1.2B, Part2.N$287
  N15: Pololu_A1.GND#14, Part2.N$313
  N16: Pololu_A1.VMOT, Part2.N$511
  N17: Part2.D7, J1.vcc
  N18: Part2.N$549, M1.D
  N19: Part2.N$550, M1.B
  N20: Part2.N$551, M1.C
  N21: Part2.N$552, M1.A

notes:
  MG996R Metal Gear Servo
  SG92r servo
  12v PSU
  A4988 Driver
  Arduino UNO
  CNC Shield
  Limit Switch
  Nema 17
  BreadBoard
