# Fritzing sketch iot (saved by Fritzing 0.9.5d)

parts:
  Gizwits_WiFi_Witty_ESP-12F1 = Gizwits WiFi Witty ESP-12F
  hc-sr1 = hc-sr04
  hc-sr2 = hc-sr04
  hc-sr3 = hc-sr04

nets:
  N1: Gizwits_WiFi_Witty_ESP-12F1.GND, hc-sr3.Echo
  N2: Gizwits_WiFi_Witty_ESP-12F1.GPIO15, hc-sr3.Trig
  N3: Gizwits_WiFi_Witty_ESP-12F1.GPIO2, hc-sr2.Echo
  N4: Gizwits_WiFi_Witty_ESP-12F1.GPIO0, hc-sr2.Trig
  GND: Gizwits_WiFi_Witty_ESP-12F1.GPIO4, hc-sr1.GND, hc-sr2.GND, hc-sr3.GND
  N5: Gizwits_WiFi_Witty_ESP-12F1.GPIO5, hc-sr1.Echo
  N6: Gizwits_WiFi_Witty_ESP-12F1.RXD, hc-sr1.Trig
  VCC: Gizwits_WiFi_Witty_ESP-12F1.TXD, hc-sr1.VCC, hc-sr2.VCC, hc-sr3.VCC

notes:
  ESP32 WROOM
  Ultrasonic Sensor(Bin 1)
  Ultrasonic Sensor(Bin 3)
  Ultrasonic Sensor(Bin 2)
